// Digital circuit hw3_a.dig as structural Verilog
module hw3_a (
  input  clk,
  input  X,
  input  Y,
  output out_2
);

  wire comparator_1_eq, multiplexer_1_out;

  Comparator comparator_1 (.a(1'b0), .b(X), .eq(comparator_1_eq));  // open: gt, lt
  Multiplexer multiplexer_1 (.sel(comparator_1_eq), .in_0(Y), .in_1(X), .out(multiplexer_1_out));
  Register register_1 (.D(multiplexer_1_out), .C(clk), .en(1'b1), .Q(out_2));
endmodule
