// Digital circuit hw3_b.dig as structural Verilog
module hw3_b (
  input  clk,
  input  X,
  input  Y
);

  wire add_1_s, comparator_1_eq, multiplexer_1_out, register_1_q;

  Add add_1 (.a(X), .b(Y), .c_i(1'b0), .s(add_1_s));  // open: c_o
  Comparator comparator_1 (.a(Y), .b(X), .eq(comparator_1_eq));  // open: gt, lt
  Multiplexer multiplexer_1 (.sel(comparator_1_eq), .in_0(add_1_s), .in_1(Y), .out(multiplexer_1_out));
  Register register_1 (.D(multiplexer_1_out), .C(clk), .en(1'b1), .Q(register_1_q));
  // Probe on register_1_q
endmodule
