// Digital circuit hw3_c.dig as structural Verilog
module hw3_c (
  input  clk
);

  wire X_lt_Y_lt;
  wire [3:0] multiplexer_1_out, register_1_q, X_plus_4_s, Y_plus_6_s;

  Add #(.Bits(4)) Y_plus_6 (.a(4'b0110), .b(4'b0001), .c_i(1'b0), .s(Y_plus_6_s));  // open: c_o
  Add #(.Bits(4)) X_plus_4 (.a(4'b0100), .b(4'b0011), .c_i(1'b0), .s(X_plus_4_s));  // open: c_o
  Comparator #(.Bits(4)) X_lt_Y (.a(4'b0011), .b(4'b0001), .lt(X_lt_Y_lt));  // open: gt, eq
  Multiplexer #(.Bits(4)) multiplexer_1 (
    .sel(X_lt_Y_lt), .in_0(Y_plus_6_s), .in_1(X_plus_4_s), .out(multiplexer_1_out));
  Register #(.Bits(4)) register_1 (.D(multiplexer_1_out), .C(clk), .en(1'b1), .Q(register_1_q));
  // Probe on register_1_q
endmodule
