// Digital circuit hw3_d.dig as structural Verilog
module hw3_d (
  input  clk
);

  wire X_gt_Y_gt;
  wire [3:0] multiplexer_1_out, register_1_q, X_plus_5_s, X_plus_6_s;

  Add #(.Bits(4)) X_plus_6 (.a(4'b0110), .b(4'b0011), .c_i(1'b0), .s(X_plus_6_s));  // open: c_o
  Add #(.Bits(4)) X_plus_5 (.a(4'b0101), .b(4'b0011), .c_i(1'b0), .s(X_plus_5_s));  // open: c_o
  Comparator #(.Bits(4)) X_gt_Y (.a(4'b0011), .b(4'b0001), .gt(X_gt_Y_gt));  // open: eq, lt
  Multiplexer #(.Bits(4)) multiplexer_1 (
    .sel(X_gt_Y_gt), .in_0(X_plus_6_s), .in_1(X_plus_5_s), .out(multiplexer_1_out));
  Register #(.Bits(4)) register_1 (.D(multiplexer_1_out), .C(clk), .en(1'b1), .Q(register_1_q));
  // Probe on register_1_q
endmodule
